# Fritzing sketch wiring (saved by Fritzing 0.9.9b)
breadboards: 1

parts:
  J1 = STM32 Nucleo boards
  M1 = RioRand LM2596
  Part1 = InvenSense MPU6050
  M2 = DC Motor
  M3 = DC Motor
  Part2 = Motor Driver 1A Dual TB6612FNG
  VCC1 = Battery block 9V

nets:
  N1: J1.PB11, Part2.AIN2
  N2: J1.JP5_03, M1.Pin_3
  N3: J1.A4/SDA, Part1.SDA, Part1.XDA
  N4: J1.A5/SCL, Part1.SCL
  3V3: J1.3V3, Part1.VCC
  N5: J1.GND#1188, M1.Pin_4
  N6: J1.GND#1189, Part1.GND
  N7: J1.PB10, Part2.AIN1
  N8: J1.PA0, Part2.BIN1
  N9: J1.PA1, Part2.BIN2
  N10: M1.Pin_1, Part2.VCC, VCC1.+
  N11: M1.Pin_2, Part2.GND, VCC1.-
  N12: M2.pin_1, Part2.A02
  N13: M2.pin_2, Part2.A01
  N14: M3.pin_1, Part2.B01
  N15: M3.pin_2, Part2.B02

notes:
  Encoder power +
  -
  Signal A B
